# Fritzing sketch Schematic_Crousel (saved by Fritzing 0.7.10b)
breadboards: 1

parts:
  LED1 = LED - 5mm [color="Red (633nm)" package="5 mm [THT]"]
  LED3 = LED - 5mm [color="Green (560nm)" package="5 mm [THT]"]
  Arduino1 = Arduino
  Part1 = Arduino Power Driver Shield
  R1 = Resistor [tolerance=±5% resistance=330 package=THT]
  R2 = Resistor [tolerance=±5% resistance=330 package=THT]
  LED2 = LED - 5mm [color="Yellow (595nm)" package="5 mm [THT]"]
  LED4 = LED - 5mm [color="Infrared (850nm)" package="5 mm [THT]"]
  R4 = Resistor [tolerance=±5% resistance=150 package=THT]
  R5 = Resistor [tolerance=±5% resistance=150 package=THT]
  R6 = Resistor [tolerance=±5% resistance=150 package=THT]
  U1 = mystery part, 3 pins [chip_label=?]
  LED5 = LED - 5mm [color="Infrared (850nm)" package="5 mm [THT]"]
  U2 = mystery part, 3 pins [chip_label=?]
  S1 = Pushbutton [package="[THT]"]
  S2 = Pushbutton [package="[THT]"]
  U3 = mystery part, 6 pins [chip_label=?]
  LED6 = LED - 5mm [color="Infrared (850nm)" package="5 mm [THT]"]
  U4 = mystery part, 3 pins [chip_label=?]
  R7 = Resistor [tolerance=±5% resistance=330 package=THT]

nets:
  N1: LED1.cathode, LED3.cathode, Part1.GND, LED2.cathode, LED5.cathode, S1.Pin_3, S1.Pin_4, S2.Pin_3, S2.Pin_4, U3.pin4
  N2: LED1.anode, R4.Pin_0
  N3: LED3.anode, R6.Pin_0
  N4: Arduino1.D11, Part1.D11
  N5: Arduino1.D10, Part1.D10
  N6: Arduino1.D9, Part1.D9
  N7: Arduino1.D6, Part1.D6
  N8: Arduino1.D5, Part1.D5
  N9: Arduino1.D3, Part1.D3
  N10: Arduino1.+5V, Part1.5V_ARDUINO, R1.Pin_0, R2.Pin_0, U1.pin3, U2.pin3, U3.pin3, R7.Pin_0
  N11: Part1.A0, U1.pin2
  N12: Part1.A1, U2.pin2
  N13: Part1.A2, U4.pin2
  N14: Part1.A3, R4.Pin_1
  N15: Part1.A4, R5.Pin_1
  N16: Part1.A5, R6.Pin_1
  N17: Part1.D2, S1.Pin_1, S1.Pin_2
  N18: Part1.D4, S2.Pin_1, S2.Pin_2
  N19: Part1.D7, U3.pin1
  N20: Part1.D8, U3.pin6
  N21: Part1.RX, U3.pin2
  N22: Part1.TX, U3.pin5
  N23: R1.Pin_1, LED4.anode
  N24: R2.Pin_1, LED5.anode
  N25: LED2.anode, R5.Pin_0
  N26: LED4.cathode, U1.pin1
  N27: LED6.anode, R7.Pin_1

notes:
  Photointerruptor Upper
  Photointerruptor Lower
  Red
  Green
  As viewed from front of machine (plug side)
  GND
  INI TEST
  BUSY
  5v
  PASS/FAIL
  ERROR
  Solenoid Upper Gate
  Pneu Bottom Advance
  Pneu Upper Advance
  Pneu Board Press
  Photointerruptor Carraige
